// Logisim project Circuit.circ as structural Verilog: 3 circuits, main circuit D-Flip-Flop
module D_Flip_Flop (
  input  in_1,
  input  in_2,
  output out_3,
  output out_4
);

  wire and_1_out, and_2_out, and_3_out, and_4_out, nor_1_out, nor_2_out;

  and and_1 (and_1_out, in_1, in_2);
  and and_2 (and_2_out, in_2, ~in_1);  // AND_Gate
  nor nor_1 (nor_1_out, and_1_out, nor_2_out);
  nor nor_2 (nor_2_out, nor_1_out, and_2_out);
  and and_3 (and_3_out, ~in_2, nor_1_out);  // AND_Gate
  and and_4 (and_4_out, nor_2_out, ~in_2);  // AND_Gate
  nor nor_3 (out_3, and_3_out, out_4);
  nor nor_4 (out_4, out_3, and_4_out);
endmodule

module Rod_Controller (
  input  DIR,
  input  GO,
  input  ESTOP,
  input  TOP,
  input  BOTM,
  output UP,
  output DOWN
);

  wire and_1_out, and_2_out, and_3_out, and_4_out, and_5_out, d_ff_1_out_3, d_ff_2_out_3, or_1_out, xor_1_out;

  xor xor_1 (xor_1_out, and_5_out, d_ff_2_out_3);
  D_Flip_Flop d_ff_1 (.in_1(xor_1_out), .in_2(GO), .out_3(d_ff_1_out_3));  // open: out_4
  or or_1 (or_1_out, UP, DOWN);
  D_Flip_Flop d_ff_2 (.in_1(or_1_out), .in_2(ESTOP), .out_3(d_ff_2_out_3));  // open: out_4
  and and_1 (and_1_out, ~DIR, d_ff_1_out_3, ~d_ff_2_out_3, ~TOP, ~BOTM);  // AND_Gate
  and and_2 (and_2_out, ~DIR, d_ff_1_out_3, ~d_ff_2_out_3, ~TOP, BOTM);  // AND_Gate
  and and_3 (and_3_out, DIR, d_ff_1_out_3, ~d_ff_2_out_3, ~TOP, ~BOTM);  // AND_Gate
  and and_4 (and_4_out, DIR, d_ff_1_out_3, ~d_ff_2_out_3, TOP, ~BOTM);  // AND_Gate
  or or_2 (UP, and_1_out, and_2_out);
  and and_5 (and_5_out, ~UP, ~DOWN);  // AND_Gate
  or or_3 (DOWN, and_3_out, and_4_out);
endmodule

module Rod_Insertion (
  input  DIR,
  input  GO,
  input  ESTOP,
  input  TOP,
  input  BOTM,
  output UP,
  output DOWN
);

  wire and_2_out, d_ff_1_out_3, d_ff_2_out_3, or_1_out, xor_1_out;

  xor xor_1 (xor_1_out, and_2_out, d_ff_2_out_3);
  D_Flip_Flop d_ff_1 (.in_1(xor_1_out), .in_2(GO), .out_3(d_ff_1_out_3));  // open: out_4
  or or_1 (or_1_out, UP, DOWN);
  D_Flip_Flop d_ff_2 (.in_1(or_1_out), .in_2(ESTOP), .out_3(d_ff_2_out_3));  // open: out_4
  and and_1 (UP, ~DIR, d_ff_1_out_3, ~d_ff_2_out_3, ~TOP);  // AND_Gate
  and and_2 (and_2_out, ~UP, ~DOWN);  // AND_Gate
  and and_3 (DOWN, DIR, d_ff_1_out_3, ~d_ff_2_out_3, ~BOTM);  // AND_Gate
endmodule
