// Logisim project Lab13.circ as structural Verilog: 6 circuits, main circuit main
module main (
  input  DIR,
  input  GO,
  input  ESTOP,
  input  TOP,
  input  BOTM,
  output MOTOR_UP,
  output MOTOR_DOWN
);

  Controller controller_1 (.DIR(DIR), .GO(GO), .ESTOP(ESTOP), .TOP(TOP), .BOTM(BOTM), .UP(MOTOR_UP), .DOWN(MOTOR_DOWN));
endmodule

module SR_Latch (
  input  RESET,
  input  SET,
  output out_3
);

  wire or_1_out;

  or or_1 (or_1_out, out_3, SET);
  and and_1 (out_3, ~RESET, or_1_out);  // AND_Gate
endmodule

module FSM (
  input  GO,
  input  ESTOP,
  output out_3
);

  wire sequential_1_out_3;

  Sequential sequential_1 (.GO(GO), .ESTOP(ESTOP), .out_3(sequential_1_out_3));
  Combinational combinational_1 (.GO(sequential_1_out_3), .ESTOP(ESTOP), .out_3(out_3));
endmodule

module Sequential (
  input  GO,
  input  ESTOP,
  output out_3
);

  SR_Latch sr_latch_1 (.RESET(ESTOP), .SET(GO), .out_3(out_3));
endmodule

// NCTL
module Controller (
  input  DIR,
  input  GO,
  input  ESTOP,
  input  TOP,
  input  BOTM,
  output UP,
  output DOWN
);

  wire fsm_1_out_3;

  FSM fsm_1 (.GO(GO), .ESTOP(ESTOP), .out_3(fsm_1_out_3));
  and and_1 (UP, ~DIR, fsm_1_out_3, ~TOP);  // AND_Gate
  and and_2 (DOWN, DIR, fsm_1_out_3, ~BOTM);  // AND_Gate
endmodule

module Combinational (
  input  GO,
  input  ESTOP,
  output out_3
);

  and and_1 (out_3, GO, ~ESTOP);  // AND_Gate
endmodule
